# Fritzing sketch Controlando LED's (saved by Fritzing 0.9.3b)
breadboards: 1

parts:
  R1 = Resistor [tolerance=±5% resistance=220 package="0603 [SMD]"]
  Componente1 = Arduino Uno (Rev3)
  LED1 = smd LED [color="Red (633nm)" package="1206 [SMD]"]
  LED3 = smd LED [color="Green (555nm)" package="0805 [SMD]"]
  R2 = Resistor [tolerance=±5% resistance=220 package="0603 [SMD]"]
  R3 = Resistor [tolerance=±5% resistance=220 package="0603 [SMD]"]
  R4 = Resistor [tolerance=±5% resistance=220 package="0603 [SMD]"]
  LED2 = smd LED [color="Blue (430nm)" package="0805 [SMD]"]
  LED4 = smd LED [color="Yellow (585nm)" package="0805 [SMD]"]

nets:
  N1: R1.Pin_0, LED1.cathode
  N2: R1.Pin_1, Componente1.GND, R2.Pin_1, R3.Pin_1, R4.Pin_1
  N3: Componente1.D2, LED3.anode
  N4: Componente1.D3_PWM, LED4.anode
  N5: Componente1.D4, LED1.anode
  N6: Componente1.D5_PWM, LED2.anode
  N7: LED3.cathode, R2.Pin_0
  N8: R3.Pin_0, LED2.cathode
  N9: R4.Pin_0, LED4.cathode
