# Fritzing sketch O primeiro circuito electrônico (saved by Fritzing 0.9.3b)
breadboards: 1

parts:
  Componente1 = Arduino Uno (Rev3)
  M1 = DC Motor

nets:
  N1: Componente1.5V, M1.pin_1
  N2: Componente1.GND, M1.pin_2
