# Fritzing sketch O tabuleiro do Genius (saved by Fritzing 0.9.3b)
breadboards: 1

parts:
  R1 = Resistor [tolerance=±5% resistance=220 package="0603 [SMD]"]
  Componente1 = Arduino Uno (Rev3)
  LED1 = smd LED [color="Red (633nm)" package="1206 [SMD]"]
  LED3 = smd LED [color="Green (555nm)" package="0805 [SMD]"]
  R2 = Resistor [tolerance=±5% resistance=220 package="0603 [SMD]"]
  R3 = Resistor [tolerance=±5% resistance=220 package="0603 [SMD]"]
  R4 = Resistor [tolerance=±5% resistance=220 package="0603 [SMD]"]
  LED2 = smd LED [color="Blue (430nm)" package="0805 [SMD]"]
  LED4 = smd LED [color="Yellow (585nm)" package="0805 [SMD]"]
  S1 = Pushbutton [package="[THT]"]
  S2 = Pushbutton [package="[THT]"]
  S3 = Pushbutton [package="[THT]"]
  S4 = Pushbutton [package="[THT]"]
  U1 = POT [package=pot_mammoth]

nets:
  N1: R1.Pin_0, LED1.cathode
  N2: R1.Pin_1, Componente1.GND, R2.Pin_1, R3.Pin_1, R4.Pin_1, S1.Pin_1, S1.Pin_2, S2.Pin_1, S2.Pin_2, S3.Pin_1, S3.Pin_2, S4.Pin_1, S4.Pin_2, U1.S
  N3: Componente1.D8, S1.Pin_3, S1.Pin_4
  N4: Componente1.D9_PWM, S4.Pin_3, S4.Pin_4
  N5: Componente1.D10_PWM/SS, S3.Pin_3, S3.Pin_4
  N6: Componente1.D11_PWM/MOSI, S2.Pin_3, S2.Pin_4
  N7: Componente1.D2, LED3.anode
  N8: Componente1.D3_PWM, LED4.anode
  N9: Componente1.D4, LED1.anode
  N10: Componente1.D5_PWM, LED2.anode
  N11: Componente1.5V, U1.E
  N12: LED3.cathode, R2.Pin_0
  N13: R3.Pin_0, LED2.cathode
  N14: R4.Pin_0, LED4.cathode
