# Fritzing sketch Otimizando nosso circuito (saved by Fritzing 0.9.3b)
breadboards: 1

parts:
  R1 = Resistor [tolerance=±5% resistance=220 package="0603 [SMD]"]
  Componente1 = Arduino Uno (Rev3)
  LED1 = smd LED [color="Red (633nm)" package="1206 [SMD]"]

nets:
  N1: R1.Pin_0, LED1.cathode
  N2: R1.Pin_1, Componente1.GND
  N3: Componente1.D2, LED1.anode
