# Fritzing sketch Trabalhando com LED e Lei de Ohm (saved by Fritzing 0.9.3b)
breadboards: 1

parts:
  Componente1 = Arduino Uno (Rev3)
  LED1 = smd LED [color="Red (633nm)" package="0805 [SMD]"]
  R1 = Resistor [tolerance=±5% resistance=220 package="0603 [SMD]"]

nets:
  N1: Componente1.5V, LED1.anode
  N2: Componente1.GND, R1.Pin_0
  N3: LED1.cathode, R1.Pin_1
