# Fritzing sketch Visualizando de outra maneira (saved by Fritzing 0.9.3b)
breadboards: 1

parts:
  R1 = Resistor [tolerance=±5% resistance=220 package="0603 [SMD]"]
  Componente1 = Arduino Uno (Rev3)
  LED1 = smd LED [color="Red (633nm)" package="1206 [SMD]"]
  S1 = Pushbutton [package="[THT]"]
  R2 = Resistor [tolerance=±5% resistance=10 package="0603 [SMD]"]

nets:
  N1: R1.Pin_0, LED1.cathode
  N2: R1.Pin_1, Componente1.GND, S1.Pin_1, S1.Pin_2
  N3: Componente1.D10_PWM/SS, S1.Pin_3, S1.Pin_4, R2.Pin_0
  N4: Componente1.D4, LED1.anode
  N5: Componente1.5V, R2.Pin_1
